# Fritzing sketch lechuck (saved by Fritzing 0.8.3b)
circuit board: 16.9333cm x 5.64444cm

parts:
  R1 = Resistor [tolerance=±5% resistance=100 package=THT]
  S1 = Pushbutton [package="[THT]"]
  IC1 = IC, DIP package, 8 pins [chip_label="attiny 85"]
  VCC1 = Battery
  R2 = Resistor [tolerance=±5% resistance=100 package=THT]
  R3 = Resistor [tolerance=±5% resistance=100 package=THT]
  R4 = Resistor [tolerance=±5% resistance=100 package=THT]
  LED_1 = LED - 5mm [color="White (4500K)" package="5 mm [THT]"]
  LED_2 = LED - 5mm [color="White (4500K)" package="5 mm [THT]"]
  LED_3 = LED - 5mm [color="White (4500K)" package="5 mm [THT]"]
  LED_4 = LED - 5mm [color="White (4500K)" package="5 mm [THT]"]
  LED_5 = LED - 5mm [color="White (4500K)" package="5 mm [THT]"]
  LED_6 = LED - 5mm [color="White (4500K)" package="5 mm [THT]"]
  LED_7 = LED - 5mm [color="White (4500K)" package="5 mm [THT]"]
  LED_8 = LED - 5mm [color="White (4500K)" package="5 mm [THT]"]
  LED_9 = LED - 5mm [color="White (4500K)" package="5 mm [THT]"]
  LED_10 = LED - 5mm [color="White (4500K)" package="5 mm [THT]"]
  LED_11 = LED - 5mm [color="White (4500K)" package="5 mm [THT]"]
  LED_0 = smd LED [color="White (4500K)" package="1206 [SMD]"]

nets:
  N1: R1.Pin_0, IC1.pin6
  N2: R1.Pin_1, LED_1.anode, LED_6.anode, LED_7.cathode, LED_8.anode, LED_9.cathode, LED_0.cathode
  N3: S1.Pin_3, S1.Pin_4, IC1.pin4, IC1.pin5, VCC1.-
  N4: IC1.pin2, R3.Pin_0
  N5: IC1.pin3, R4.Pin_0
  N6: IC1.pin7, R2.Pin_0
  N7: IC1.pin8, VCC1.+
  N8: R2.Pin_1, LED_1.cathode, LED_2.anode, LED_3.cathode, LED_4.anode, LED_5.cathode, LED_0.anode
  N9: R3.Pin_1, LED_2.cathode, LED_3.anode, LED_6.cathode, LED_7.anode, LED_10.anode, LED_11.cathode
  N10: R4.Pin_1, LED_4.cathode, LED_5.anode, LED_8.cathode, LED_9.anode, LED_10.cathode, LED_11.anode

notes:
  LED 0
  LED 1
  LED 2
  LED 3
  LED 4
  LED 5
  LED 6
  LED 7
  LED 8
  LED 9
  LED 10
  LED 11
  Switch
