# Fritzing sketch xmas (saved by Fritzing 0.7.7b)

parts:
  R1 = Resistor [tolerance=±5% resistance=100 package=THT]
  S1 = Pushbutton [package="[THT]"]
  IC1 = IC, DIP package, 8 pins [chip_label="attiny 85"]
  VCC1 = Battery
  LED1 = LED - 5mm [color="White (4500K)" package="5 mm [THT]"]
  J1 = Piezo Speaker

nets:
  N1: R1.Pin_0, IC1.pin6
  N2: R1.Pin_1, LED1.anode
  N3: S1.Pin_3, S1.Pin_4, IC1.pin4, IC1.pin5, VCC1.-, LED1.cathode, J1.pin1
  N4: IC1.pin7, J1.pin2
  N5: IC1.pin8, VCC1.+
