# Fritzing sketch larson (saved by Fritzing 0.7.7b)

parts:
  Arduino1 = Arduino
  R1 = Resistor [tolerance=±5% resistance=560 package=THT]
  LED1 = LED - 5mm [color="Red (633nm)" package="5 mm [THT]"]
  R2 = Resistor [tolerance=±5% resistance=560 package=THT]
  LED2 = LED - 5mm [color="Red (633nm)" package="5 mm [THT]"]
  R3 = Resistor [tolerance=±5% resistance=560 package=THT]
  LED3 = LED - 5mm [color="Red (633nm)" package="5 mm [THT]"]
  R4 = Resistor [tolerance=±5% resistance=560 package=THT]
  LED4 = LED - 5mm [color="Red (633nm)" package="5 mm [THT]"]
  R5 = Resistor [tolerance=±5% resistance=560 package=THT]
  LED5 = LED - 5mm [color="Red (633nm)" package="5 mm [THT]"]
  R6 = Resistor [tolerance=±5% resistance=560 package=THT]
  LED6 = LED - 5mm [color="Red (633nm)" package="5 mm [THT]"]

nets:
  N1: Arduino1.D11, R1.Pin_0
  N2: Arduino1.D10, R2.Pin_0
  N3: Arduino1.D9, R3.Pin_0
  N4: Arduino1.D6, R4.Pin_0
  N5: Arduino1.D5, R5.Pin_0
  N6: Arduino1.D3, R6.Pin_0
  N7: Arduino1.GND, LED1.cathode, LED2.cathode, LED3.cathode, LED4.cathode, LED5.cathode, LED6.cathode
  N8: R1.Pin_1, LED1.anode
  N9: R2.Pin_1, LED2.anode
  N10: R3.Pin_1, LED3.anode
  N11: R4.Pin_1, LED4.anode
  N12: R5.Pin_1, LED5.anode
  N13: R6.Pin_1, LED6.anode
