# Fritzing sketch nightlight (saved by Fritzing 0.7.7b)
breadboards: 1

parts:
  Arduino1 = Arduino
  T1 = LM35 Temperature Sensor [package="TO92 [THT]"]
  LED2 = RGB LED (com. anode, rbg) [package="5 mm [THT]"]
  S1 = Toggle Switch [package=THT]

nets:
  GND: Arduino1.GND, T1.GND, S1.COM
  N1: Arduino1.D10, S1.L2
  N2: Arduino1.D6, LED2.blue_cathode
  N3: Arduino1.D5, LED2.green_cathode
  N4: Arduino1.D3, LED2.red_cathode
  N5: Arduino1.+5V, T1.+Vs, LED2.common_anode
  N6: Arduino1.A0, T1.Vout
